// Digital circuit 32_Comptur.dig as structural Verilog
module _32_Comptur (
  input  [31:0] in_1,
  input  clk,
  input  [4:0] in_3,
  input  in_4,
  input  [4:0] in_5,
  input  [4:0] in_7,
  input  [1:0] in_9,
  input  [15:0] in_10,
  input  in_11,
  input  in_12,
  output out_6,
  output [31:0] out_8
);

  wire MemWr;
  wire [4:0] multiplexer_1_out;
  wire [31:0] BusA, BusB, Ext_OUT, Mem_OUT, multiplexer_2_out;

  Multiplexer multiplexer_1 (.in_0(in_7[0]), .in_1(in_5[0]), .out(multiplexer_1_out[0]));  // open: sel
  RegisterFile #(.AddrBits(5), .Bits(32)) registerfile_1 (
    .Din(in_1), .we(in_4), .Rw(multiplexer_1_out), .C(clk), .Ra(in_3), .Rb(in_7), .Da(BusA), .Db(BusB));
  // Extender extender_1: pin names not known; wires that end beside it: in_10, in_12, Ext_OUT
  Multiplexer #(.Bits(32)) multiplexer_2 (.sel(in_11), .in_0(BusB), .in_1(Ext_OUT), .out(multiplexer_2_out));
  ALU alu_1 (.ALU_CTR(in_9), .A(BusA), .B(multiplexer_2_out), .OUT(out_8), .ZERO(out_6));
  BlockRAMDualPort #(.AddrBits(5), .Bits(32)) Date_Nenory (
    .A(out_8[4:0]), .Din(BusB), .str(MemWr), .C(clk), .D(Mem_OUT));
  Multiplexer multiplexer_3 (.in_0(out_8[0]), .in_1(Mem_OUT[0]), .out(in_1[0]));  // open: sel
  // Pins of 1 and 32 bits meet at in_1
  // Pins of 1 and 5 bits meet at multiplexer_1_out
  // Pins of 1 and 5 bits meet at in_7
  // Pins of 1 and 5 bits meet at in_5
  // Pins of 1 and 5 and 32 bits meet at out_8
  // Pins of 1 and 32 bits meet at Mem_OUT

  // Other names for the same wires on the sheet: ALU_OUT[31:0] = out_8; ALUctr[1:0] = in_9; ALUSrc = in_11;
  //   BusW[31:0] = in_1; ExtOp = in_12; imm16[15:0] = in_10; Rd[4:0] = in_5; RegWr = in_4; Rs[4:0] = in_3;
  //   Rt[4:0] = in_7; Zero = out_6

  // Notes on the sheet:
  //   32-bit
  //   Registers
endmodule
