// Digital circuit 32_Computer.dig as structural Verilog
module _32_Computer (
  input  clk,
  output [31:0] out_2
);

  wire ALU_Src, Branch, Ext_Op, J_CTR, J_CTR1, Jal_ctr, Mem_Re, Mem_Wr, MemtoReg, or_1_out, pullup_1_out,
       pullup_2_out, Reg_Dst, Reg_Wr, Zero;
  wire [2:0] ALU_ctr, ALU_Op;
  wire [4:0] multiplexer_2_out;
  wire [23:0] barrelshifter_1_out;
  wire [31:0] add_1_s, ALU_RES, Bus_A, Bus_B, Bus_W, Ext_OUT, Mem_OUT, multiplexer_1_out, multiplexer_3_out,
       PC_Counter;

  BarrelShifter #(.Bits(24), .direction("right")) barrelshifter_1 (
    .in(PC_Counter[23:0]), .shift(5'b00010), .out(barrelshifter_1_out));
  PullUp pullup_1 (.out(pullup_1_out));
  ROM #(.AddrBits(24), .Bits(32)) rom_1 (.A(barrelshifter_1_out), .sel(pullup_1_out), .D(out_2));
  or or_1 (or_1_out, J_CTR1, J_CTR);
  Control control_1 (
    .OP_CODE(out_2[31:26]), .RegDst(Reg_Dst), .ALUSrc(ALU_Src), .MemToReg(MemtoReg), .RegWrite(Reg_Wr),
    .MemRead(Mem_Re), .MemWrite(Mem_Wr), .Branch(Branch), .ALUOp(ALU_Op), .JaL_CRT(Jal_ctr), .J_CRT(J_CTR1),
    .ExtOp(Ext_Op));
  PC pc_1 (
    .OUT(PC_Counter), .imm16(out_2[15:0]), .RegD(ALU_RES), .J_CTR(or_1_out), .Branch(Branch), .Zero(Zero),
    .CLK(clk), .En(pullup_2_out));
  PullUp pullup_2 (.out(pullup_2_out));
  Add #(.Bits(32)) add_1 (.a(PC_Counter), .b(32'h4), .c_i(1'b0), .s(add_1_s));  // open: c_o
  Multiplexer #(.Bits(32)) multiplexer_1 (.sel(Jal_ctr), .in_0(Bus_W), .in_1(add_1_s), .out(multiplexer_1_out));
  Multiplexer #(.Bits(5)) multiplexer_2 (
    .sel(Reg_Dst), .in_0(out_2[20:16]), .in_1(out_2[15:11]), .out(multiplexer_2_out));
  // instruction_memory instruction_memory_1: pin names not known; wires that end beside it: PC_Counter[23:0]
  // Extender extender_1: pin names not known; wires that end beside it: out_2[15:0], Ext_Op, Ext_OUT
  RegisterFile #(.AddrBits(5), .Bits(32)) registerfile_1 (
    .Din(multiplexer_1_out), .we(Reg_Wr), .Rw(multiplexer_2_out), .C(clk), .Ra(out_2[25:21]),
    .Rb(out_2[20:16]), .Da(Bus_A), .Db(Bus_B));
  ALU_Controll alu_controll_1 (.ALU_Op(ALU_Op), .func(out_2[5:0]), .ALU_CTR(ALU_ctr), .J_CTR(J_CTR));
  Multiplexer #(.Bits(32)) multiplexer_3 (.sel(ALU_Src), .in_0(Bus_B), .in_1(Ext_OUT), .out(multiplexer_3_out));
  ALU alu_1 (.ALU_CTR(ALU_ctr), .A(Bus_A), .B(multiplexer_3_out), .OUT(ALU_RES), .ZERO(Zero));
  RAMDualPort #(.AddrBits(5), .Bits(32)) Data_Memory (
    .A(ALU_RES[4:0]), .Din(Bus_B), .str(Mem_Wr), .C(clk), .ld(Mem_Re), .D(Mem_OUT));
  Multiplexer #(.Bits(32)) multiplexer_4 (.sel(MemtoReg), .in_0(ALU_RES), .in_1(Mem_OUT), .out(Bus_W));
  Seven_Seg_Hex seven_seg_hex_1 (.d(Bus_A[7:4]), .dp(1'b0));
  Seven_Seg_Hex seven_seg_hex_2 (.d(Bus_B[7:4]), .dp(1'b0));
  Seven_Seg_Hex seven_seg_hex_3 (.d(ALU_RES[7:4]), .dp(1'b0));
  Seven_Seg_Hex seven_seg_hex_4 (.d(Bus_A[3:0]), .dp(1'b0));
  Seven_Seg_Hex seven_seg_hex_5 (.d(Bus_B[3:0]), .dp(1'b0));
  Seven_Seg_Hex seven_seg_hex_6 (.d(ALU_RES[3:0]), .dp(1'b0));

  // Other names for the same wires on the sheet: Func[5:0] = out_2[5:0]; imm16[15:0] = out_2[15:0];
  //   Shamt[4:0] = out_2[10:6]; Rd[4:0] = out_2[15:11]; Rt[4:0] = out_2[20:16]; Rs[4:0] = out_2[25:21];
  //   OP[5:0] = out_2[31:26]

  // Notes on the sheet:
  //   contents of rom_1 (hex, n*v repeats v):
  //   2004000a,20050000,20060001,a63820,c02820,e03020,20010001,812022
  //   ,10800001,8000003,e03820,800000a
  //   32-bit
  //   Registers
endmodule
