// Digital circuit ALU_Controll.dig as structural Verilog
module ALU_Controll (
  input  [2:0] ALU_Op,
  input  [5:0] func,
  output [2:0] ALU_ctr
);

  wire and_1_out, and_2_out, and_4_out, and_5_out, and_6_out, and_7_out, and_8_out, and_9_out;

  and and_1 (and_1_out, ~func[0], ~func[1], ~func[2], ~func[3], ~func[4], func[5], ~ALU_Op[0], ~ALU_Op[1], ALU_Op[2]);  // And
  and and_2 (and_2_out, ~func[0], func[1], ~func[2], ~func[3], ~func[4], func[5], ~ALU_Op[0], ~ALU_Op[1], ALU_Op[2]);  // And
  // And and_3 has open pins: In_1=func[0], In_2=func[1], In_3=func[2], In_4=func[3], In_5=func[4], In_6=func[5], In_7=ALU_Op[0], In_8=ALU_Op[1], In_9=ALU_Op[2], out=open
  and and_4 (and_4_out, func[0], ~func[1], func[2], ~func[3], ~func[4], func[5], ~ALU_Op[0], ~ALU_Op[1], ALU_Op[2]);  // And
  and and_5 (and_5_out, ALU_Op[0], ALU_Op[1], ~ALU_Op[2]);  // And
  and and_6 (and_6_out, ~ALU_Op[0], ALU_Op[1], ~ALU_Op[2]);  // And
  and and_7 (and_7_out, ~ALU_Op[0], ALU_Op[1], ALU_Op[2]);  // And
  and and_8 (and_8_out, ~ALU_Op[0], ~ALU_Op[1], ~ALU_Op[2]);  // And
  and and_9 (and_9_out, ~ALU_Op[0], ~ALU_Op[1], ~ALU_Op[2]);  // And
  or or_1 (ALU_ctr[2], and_2_out, and_7_out);
  or or_2 (ALU_ctr[1], and_1_out, and_2_out, and_5_out, and_7_out, and_8_out, and_9_out);
  or or_3 (ALU_ctr[0], and_6_out, and_4_out);

  // Notes on the sheet:
  //   add
  //   sub
  //   and
  //   or
  //   addi
  //   ori
  //   beq
  //   lw
  //   sw
  //   ALUCre[2]
  //   ALUCre[1]
  //   ALUCre[0]
endmodule
