// Digital circuit Control.dig as structural Verilog
module Control (
  input  [5:0] OP_CODE,
  output RegDst,
  output ALUSrc,
  output MemToReg,
  output RegWrite,
  output MemRead,
  output MemWrite,
  output Branch,
  output J_CRT,
  output [2:0] ALUOp,
  output ExtOp,
  output JaL_CRT
);

  wire and_1_out, and_2_out, and_3_out, and_4_out, and_5_out, and_6_out, and_7_out, and_8_out, and_9_out;

  and and_1 (and_1_out, ~OP_CODE[0], ~OP_CODE[1], ~OP_CODE[2], ~OP_CODE[3], ~OP_CODE[4], ~OP_CODE[5]);  // And
  and and_2 (and_2_out, ~OP_CODE[0], ~OP_CODE[1], ~OP_CODE[2], OP_CODE[3], ~OP_CODE[4], ~OP_CODE[5]);  // And
  and and_3 (and_3_out, ~OP_CODE[0], ~OP_CODE[1], OP_CODE[2], OP_CODE[3], ~OP_CODE[4], ~OP_CODE[5]);  // And
  and and_4 (and_4_out, OP_CODE[0], ~OP_CODE[1], OP_CODE[2], OP_CODE[3], ~OP_CODE[4], ~OP_CODE[5]);  // And
  and and_5 (and_5_out, ~OP_CODE[0], ~OP_CODE[1], OP_CODE[2], ~OP_CODE[3], ~OP_CODE[4], ~OP_CODE[5]);  // And
  and and_6 (and_6_out, ~OP_CODE[0], OP_CODE[1], ~OP_CODE[2], ~OP_CODE[3], ~OP_CODE[4], ~OP_CODE[5]);  // And
  and and_7 (and_7_out, OP_CODE[0], OP_CODE[1], ~OP_CODE[2], ~OP_CODE[3], ~OP_CODE[4], ~OP_CODE[5]);  // And
  and and_8 (and_8_out, OP_CODE[0], OP_CODE[1], ~OP_CODE[2], ~OP_CODE[3], ~OP_CODE[4], OP_CODE[5]);  // And
  and and_9 (and_9_out, OP_CODE[0], OP_CODE[1], ~OP_CODE[2], OP_CODE[3], ~OP_CODE[4], OP_CODE[5]);  // And
  or or_1 (RegDst, and_1_out, 1'b0);
  or or_2 (ALUSrc, and_2_out, and_3_out, and_4_out, and_6_out, and_7_out, and_8_out, and_9_out);
  or or_3 (MemToReg, and_8_out, 1'b0);
  or or_4 (RegWrite, and_1_out, and_2_out, and_3_out, and_4_out, and_7_out, and_8_out);
  or or_5 (MemRead, and_8_out, 1'b0);
  or or_6 (MemWrite, and_9_out, 1'b0);
  or or_7 (Branch, and_5_out, 1'b0);
  or or_8 (ALUOp[0], and_3_out, 1'b0);
  or or_9 (ALUOp[1], and_3_out, and_4_out, and_5_out);
  or or_10 (ALUOp[2], and_1_out, and_5_out);
  or or_11 (JaL_CRT, and_7_out, 1'b0);
  or or_12 (J_CRT, and_6_out, and_7_out);
  or or_13 (ExtOp, and_2_out, and_5_out, and_8_out, and_9_out);

  // Notes on the sheet:
  //   R-Type
  //   Add
  //   Imm
  //   And
  //   Imm
  //   Or
  //   Imm
  //   BEQ
  //   JUMP
  //   JNL
  //   LW
  //   SW
  //   RegDst
  //   ALUSrc
  //   MemToReg
  //   RegWrite
  //   MemRead
  //   MemWrite
  //   Branch
  //   ALUOp[0]
  //   ALUOp[1]
  //   ALUOp[2]
  //   JaL_CTR
  //   J_CTR
  //   ExtOp
endmodule
