// Digital circuit PC.dig as structural Verilog
module PC (
  input  [15:0] imm16,
  input  Jal_ctr,
  input  En,
  input  CLK,
  input  Branch,
  input  Zero,
  output [31:0] OUT
);

  wire and_1_out, or_1_out, pulldown_1_out, pulldown_2_out;
  wire [15:0] barrelshifter_1_out;
  wire [31:0] add_1_s, add_2_s, extender_1_p3, multiplexer_1_out;

  BarrelShifter #(.Bits(16)) barrelshifter_1 (.in(imm16), .shift(5'b00010), .out(barrelshifter_1_out));
  // Extender extender_1: pin names not known; wires that end beside it: barrelshifter_1_out, 1'b1, extender_1_p3
  PullDown pulldown_1 (.out(pulldown_1_out));
  PullDown pulldown_2 (.out(pulldown_2_out));
  Add #(.Bits(32)) add_1 (.a(OUT), .b(32'h4), .c_i(pulldown_1_out), .s(add_1_s));  // open: c_o
  Add #(.Bits(32)) add_2 (.a(add_1_s), .b(extender_1_p3), .c_i(pulldown_2_out), .s(add_2_s));  // open: c_o
  and and_1 (and_1_out, Zero, Branch);
  or or_1 (or_1_out, Jal_ctr, and_1_out);
  Multiplexer #(.Bits(32)) multiplexer_1 (.sel(or_1_out), .in_0(add_1_s), .in_1(add_2_s), .out(multiplexer_1_out));
  Register #(.Bits(32)) register_1 (.D(multiplexer_1_out), .C(CLK), .en(En), .Q(OUT));
endmodule
