// Digital circuit instruction_memory.dig as structural Verilog
module instruction_memory (
  input  [23:0] A,
  output [31:0] D,
  output [5:0] OP,
  output [4:0] Rt,
  output [4:0] Rs,
  output [4:0] Rd,
  output [4:0] Shamt,
  output [5:0] Func,
  output [15:0] imm16
);

  wire pullup_1_out;
  wire [23:0] barrelshifter_1_out;

  BarrelShifter #(.Bits(24), .direction("right")) barrelshifter_1 (.in(A), .shift(5'b00010), .out(barrelshifter_1_out));
  ROM #(.AddrBits(24), .Bits(32)) rom_1 (.A(barrelshifter_1_out), .sel(pullup_1_out), .D(D));
  PullUp pullup_1 (.out(pullup_1_out));

  assign Func = D[5:0];
  assign imm16 = D[15:0];
  assign OP = D[31:26];
  assign Rd = D[15:11];
  assign Rs = D[25:21];
  assign Rt = D[20:16];
  assign Shamt = D[10:6];

  // Notes on the sheet:
  //   contents of rom_1 (hex, n*v repeats v):
  //   201300fd,ac137f01,8c147f00,20010011,2002000b,221820,222022,222825
  //   ,223024,20090000,200a0005,112afff4,21290001,800000b
endmodule
